// Logisim project Full Adder.circ as structural Verilog
// Sum
module main (
  input  Increment,
  input  Reset,
  input  Load,
  input  [15:0] in_4,
  output [15:0] out_5
);

  wire clock_1_out;

  Clock clock_1 (.out(clock_1_out));
  Program_Counter__16_Bit program_counter_16_bit_1 (
    .Increment(Increment), .Reset(Reset), .Load(Load), .Set(in_4), .Clock(clock_1_out), .Out(out_5));
endmodule

module Full_adder (
  input  c,
  input  A,
  input  B,
  output Sum,
  output Carry
);

  wire and_1_out, and_2_out, and_3_out, and_4_out, and_5_out, and_6_out, and_7_out, not_1_out, not_2_out,
       not_3_out, not_4_out, not_5_out, not_6_out;

  not not_1 (not_1_out, c);
  not not_2 (not_2_out, A);
  not not_3 (not_3_out, c);
  not not_4 (not_4_out, B);
  not not_5 (not_5_out, A);
  not not_6 (not_6_out, B);
  and and_1 (and_1_out, A, B);
  and and_2 (and_2_out, c, B);
  and and_3 (and_3_out, c, A);
  and and_4 (and_4_out, not_1_out, not_2_out, B);
  and and_5 (and_5_out, not_3_out, A, not_4_out);
  and and_6 (and_6_out, c, not_5_out, not_6_out);
  and and_7 (and_7_out, c, A, B);
  or or_1 (Carry, and_1_out, and_2_out, and_3_out);
  or or_2 (Sum, and_4_out, and_5_out, and_6_out, and_7_out);
endmodule

module Half_adder (
  input  A,
  input  B,
  output Sum,
  output carry
);

  xor xor_1 (Sum, A, B);
  and and_1 (carry, B, A);
endmodule

module Full_adder_less_complex (
  input  c,
  input  A,
  input  B,
  output Sum,
  output Carry
);

  wire and_1_out, and_2_out, and_3_out, xor_1_out, xor_2_out;

  xor xor_1 (xor_1_out, A, B);
  xor xor_2 (xor_2_out, c, xor_1_out);
  and and_1 (and_1_out, B, A);
  and and_2 (and_2_out, xor_1_out, c);
  and and_3 (and_3_out, c, and_1_out);
  or or_1 (Carry, and_1_out, and_2_out);
  or or_2 (Sum, xor_2_out, and_3_out);
endmodule

module _8_bit_adder (
  input  [7:0] A,
  input  [7:0] B,
  output [7:0] Out
);

  wire full_adder_1_carry, full_adder_2_carry, full_adder_3_carry, full_adder_4_carry, full_adder_5_carry,
       full_adder_6_carry, half_adder_1_carry;

  Half_adder half_adder_1 (.A(A[0]), .B(B[0]), .Sum(Out[0]), .carry(half_adder_1_carry));
  Full_adder full_adder_1 (.c(half_adder_1_carry), .A(A[1]), .B(B[1]), .Sum(Out[1]), .Carry(full_adder_1_carry));
  Full_adder full_adder_2 (.c(full_adder_1_carry), .A(A[2]), .B(B[2]), .Sum(Out[2]), .Carry(full_adder_2_carry));
  Full_adder full_adder_3 (.c(full_adder_2_carry), .A(A[3]), .B(B[3]), .Sum(Out[3]), .Carry(full_adder_3_carry));
  Full_adder full_adder_4 (.c(full_adder_3_carry), .A(A[4]), .B(B[4]), .Sum(Out[4]), .Carry(full_adder_4_carry));
  Full_adder full_adder_5 (.c(full_adder_4_carry), .A(A[5]), .B(B[5]), .Sum(Out[5]), .Carry(full_adder_5_carry));
  Full_adder full_adder_6 (.c(full_adder_5_carry), .A(A[6]), .B(B[6]), .Sum(Out[6]), .Carry(full_adder_6_carry));
  Full_adder full_adder_7 (.c(full_adder_6_carry), .A(A[7]), .B(B[7]), .Sum(Out[7]));  // open: Carry
endmodule

module AND16 (
  input  [15:0] A,
  input  [15:0] B,
  output [15:0] Out
);

  and and_1 (Out[0], A[0], B[0]);
  and and_2 (Out[1], A[1], B[1]);
  and and_3 (Out[2], A[2], B[2]);
  and and_4 (Out[3], A[3], B[3]);
  and and_5 (Out[4], A[4], B[4]);
  and and_6 (Out[5], A[5], B[5]);
  and and_7 (Out[6], A[6], B[6]);
  and and_8 (Out[7], A[7], B[7]);
  and and_9 (Out[8], A[8], B[8]);
  and and_10 (Out[9], A[9], B[9]);
  and and_11 (Out[10], A[10], B[10]);
  and and_12 (Out[11], A[11], B[11]);
  and and_13 (Out[12], A[12], B[12]);
  and and_14 (Out[13], A[13], B[13]);
  and and_15 (Out[14], A[14], B[14]);
  and and_16 (Out[15], A[15], B[15]);
endmodule

module _16_bit_adder (
  input  [15:0] A,
  input  [15:0] B,
  output [15:0] Out
);

  wire full_adder_1_carry, full_adder_2_carry, full_adder_3_carry, full_adder_4_carry, full_adder_5_carry,
       full_adder_6_carry, full_adder_7_carry, full_adder_8_carry, full_adder_9_carry, full_adder_10_carry,
       full_adder_11_carry, full_adder_12_carry, full_adder_13_carry, full_adder_14_carry, half_adder_1_carry;

  Half_adder half_adder_1 (.A(A[0]), .B(B[0]), .Sum(Out[0]), .carry(half_adder_1_carry));
  Full_adder full_adder_1 (.c(half_adder_1_carry), .A(A[1]), .B(B[1]), .Sum(Out[1]), .Carry(full_adder_1_carry));
  Full_adder full_adder_2 (.c(full_adder_1_carry), .A(A[2]), .B(B[2]), .Sum(Out[2]), .Carry(full_adder_2_carry));
  Full_adder full_adder_3 (.c(full_adder_2_carry), .A(A[3]), .B(B[3]), .Sum(Out[3]), .Carry(full_adder_3_carry));
  Full_adder full_adder_4 (.c(full_adder_3_carry), .A(A[4]), .B(B[4]), .Sum(Out[4]), .Carry(full_adder_4_carry));
  Full_adder full_adder_5 (.c(full_adder_4_carry), .A(A[5]), .B(B[5]), .Sum(Out[5]), .Carry(full_adder_5_carry));
  Full_adder full_adder_6 (.c(full_adder_5_carry), .A(A[6]), .B(B[6]), .Sum(Out[6]), .Carry(full_adder_6_carry));
  Full_adder full_adder_7 (.c(full_adder_6_carry), .A(A[7]), .B(B[7]), .Sum(Out[7]), .Carry(full_adder_7_carry));
  Full_adder full_adder_8 (.c(full_adder_7_carry), .A(A[8]), .B(B[8]), .Sum(Out[8]), .Carry(full_adder_8_carry));
  Full_adder full_adder_9 (.c(full_adder_8_carry), .A(A[9]), .B(B[9]), .Sum(Out[9]), .Carry(full_adder_9_carry));
  Full_adder full_adder_10 (.c(full_adder_9_carry), .A(A[10]), .B(B[10]), .Sum(Out[10]), .Carry(full_adder_10_carry));
  Full_adder full_adder_11 (.c(full_adder_10_carry), .A(A[11]), .B(B[11]), .Sum(Out[11]), .Carry(full_adder_11_carry));
  Full_adder full_adder_12 (.c(full_adder_11_carry), .A(A[12]), .B(B[12]), .Sum(Out[12]), .Carry(full_adder_12_carry));
  Full_adder full_adder_13 (.c(full_adder_12_carry), .A(A[13]), .B(B[13]), .Sum(Out[13]), .Carry(full_adder_13_carry));
  Full_adder full_adder_14 (.c(full_adder_13_carry), .A(A[14]), .B(B[14]), .Sum(Out[14]), .Carry(full_adder_14_carry));
  Full_adder full_adder_15 (.c(full_adder_14_carry), .A(A[15]), .B(B[15]), .Sum(Out[15]));  // open: Carry
endmodule

module Incrementer16___1 (
  input  [15:0] A,
  output [15:0] Out
);

  wire full_adder_1_carry, full_adder_2_carry, full_adder_3_carry, full_adder_4_carry, full_adder_5_carry,
       full_adder_6_carry, full_adder_7_carry, full_adder_8_carry, full_adder_9_carry, full_adder_10_carry,
       full_adder_11_carry, full_adder_12_carry, full_adder_13_carry, full_adder_14_carry,
       half_adder_1_carry, not_1_out;

  not not_1 (not_1_out, 1'b1);
  Half_adder half_adder_1 (.A(A[0]), .B(1'b1), .Sum(Out[0]), .carry(half_adder_1_carry));
  Full_adder full_adder_1 (.c(half_adder_1_carry), .A(A[1]), .B(not_1_out), .Sum(Out[1]), .Carry(full_adder_1_carry));
  Full_adder full_adder_2 (.c(full_adder_1_carry), .A(A[2]), .B(not_1_out), .Sum(Out[2]), .Carry(full_adder_2_carry));
  Full_adder full_adder_3 (.c(full_adder_2_carry), .A(A[3]), .B(not_1_out), .Sum(Out[3]), .Carry(full_adder_3_carry));
  Full_adder full_adder_4 (.c(full_adder_3_carry), .A(A[4]), .B(not_1_out), .Sum(Out[4]), .Carry(full_adder_4_carry));
  Full_adder full_adder_5 (.c(full_adder_4_carry), .A(A[5]), .B(not_1_out), .Sum(Out[5]), .Carry(full_adder_5_carry));
  Full_adder full_adder_6 (.c(full_adder_5_carry), .A(A[6]), .B(not_1_out), .Sum(Out[6]), .Carry(full_adder_6_carry));
  Full_adder full_adder_7 (.c(full_adder_6_carry), .A(A[7]), .B(not_1_out), .Sum(Out[7]), .Carry(full_adder_7_carry));
  Full_adder full_adder_8 (.c(full_adder_7_carry), .A(A[8]), .B(not_1_out), .Sum(Out[8]), .Carry(full_adder_8_carry));
  Full_adder full_adder_9 (.c(full_adder_8_carry), .A(A[9]), .B(not_1_out), .Sum(Out[9]), .Carry(full_adder_9_carry));
  Full_adder full_adder_10 (
    .c(full_adder_9_carry), .A(A[10]), .B(not_1_out), .Sum(Out[10]), .Carry(full_adder_10_carry));
  Full_adder full_adder_11 (
    .c(full_adder_10_carry), .A(A[11]), .B(not_1_out), .Sum(Out[11]), .Carry(full_adder_11_carry));
  Full_adder full_adder_12 (
    .c(full_adder_11_carry), .A(A[12]), .B(not_1_out), .Sum(Out[12]), .Carry(full_adder_12_carry));
  Full_adder full_adder_13 (
    .c(full_adder_12_carry), .A(A[13]), .B(not_1_out), .Sum(Out[13]), .Carry(full_adder_13_carry));
  Full_adder full_adder_14 (
    .c(full_adder_13_carry), .A(A[14]), .B(not_1_out), .Sum(Out[14]), .Carry(full_adder_14_carry));
  Full_adder full_adder_15 (.c(full_adder_14_carry), .A(A[15]), .B(not_1_out), .Sum(Out[15]));  // open: Carry
endmodule

module ALU__16_bit (
  input  ZX,
  input  NX,
  input  ZY,
  input  NY,
  input  F,
  input  NO,
  input  [15:0] A,
  input  [15:0] B,
  output [15:0] out_9,
  output ZR,
  output NG
);

  wire or_16_1_1_out;
  wire [15:0] ADDER_out, AND16_out, Mux16_2_out_4, Mux16_3_out_4, Mux16_4_out_4, Mux16_5_out_4, Mux16_out_4,
       not_1_out, not_2_out, not_3_out, not_4_out, not_5_out;

  assign not_1_out = ~{16{1'b1}};  // NOT_Gate not_1, 16 bits wide
  Mux16 Mux16 (.A(A), .B(not_1_out), .Sel(ZX), .out_4(Mux16_out_4));
  Mux16 Mux16_2 (.A(Mux16_out_4), .B(not_2_out), .Sel(NX), .out_4(Mux16_2_out_4));
  assign not_2_out = ~Mux16_out_4;  // NOT_Gate not_2, 16 bits wide
  assign not_3_out = ~{16{1'b1}};  // NOT_Gate not_3, 16 bits wide
  Mux16 Mux16_3 (.A(B), .B(not_3_out), .Sel(ZY), .out_4(Mux16_3_out_4));
  assign not_4_out = ~Mux16_3_out_4;  // NOT_Gate not_4, 16 bits wide
  Mux16 Mux16_4 (.A(Mux16_3_out_4), .B(not_4_out), .Sel(NY), .out_4(Mux16_4_out_4));
  _16_bit_adder ADDER (.A(Mux16_2_out_4), .B(Mux16_4_out_4), .Out(ADDER_out));
  AND16 AND16 (.A(Mux16_2_out_4), .B(Mux16_4_out_4), .Out(AND16_out));
  Mux16 Mux16_5 (.A(AND16_out), .B(ADDER_out), .Sel(F), .out_4(Mux16_5_out_4));
  assign not_5_out = ~Mux16_5_out_4;  // NOT_Gate not_5, 16 bits wide
  OR_16_1 or_16_1_1 (.in_1({NG, out_9[14:0]}), .out(or_16_1_1_out));
  not not_6 (ZR, or_16_1_1_out);
  Mux16 Mux16_6 (.A(Mux16_5_out_4), .B(not_5_out), .Sel(NO), .out_4({NG, out_9[14:0]}));

  assign out_9[15] = NG;
endmodule

module OR16 (
  input  [15:0] A,
  input  [15:0] B,
  output [15:0] Out
);

  or or_1 (Out[0], A[0], B[0]);
  or or_2 (Out[1], A[1], B[1]);
  or or_3 (Out[2], A[2], B[2]);
  or or_4 (Out[3], A[3], B[3]);
  or or_5 (Out[4], A[4], B[4]);
  or or_6 (Out[5], A[5], B[5]);
  or or_7 (Out[6], A[6], B[6]);
  or or_8 (Out[7], A[7], B[7]);
  or or_9 (Out[8], A[8], B[8]);
  or or_10 (Out[9], A[9], B[9]);
  or or_11 (Out[10], A[10], B[10]);
  or or_12 (Out[11], A[11], B[11]);
  or or_13 (Out[12], A[12], B[12]);
  or or_14 (Out[13], A[13], B[13]);
  or or_15 (Out[14], A[14], B[14]);
  or or_16 (Out[15], A[15], B[15]);
endmodule

module Mux_4 (
  input  A,
  input  B,
  input  C,
  input  D,
  input  Sel_0,
  input  Sel_1,
  output Out
);

  wire and_1_out, and_2_out, and_3_out, and_4_out, not_1_out, not_2_out, not_3_out, not_4_out;

  not not_1 (not_1_out, Sel_0);
  not not_2 (not_2_out, Sel_1);
  not not_3 (not_3_out, Sel_0);
  not not_4 (not_4_out, Sel_1);
  and and_1 (and_1_out, A, not_1_out, not_2_out);
  and and_2 (and_2_out, B, not_3_out, Sel_1);
  and and_3 (and_3_out, C, Sel_0, not_4_out);
  and and_4 (and_4_out, D, Sel_0, Sel_1);
  or or_1 (Out, and_1_out, and_2_out, and_3_out, and_4_out);
endmodule

module Mux (
  input  A,
  input  B,
  input  Sel,
  output Out
);

  wire and_1_out, and_2_out, not_1_out;

  not not_1 (not_1_out, Sel);
  and and_1 (and_1_out, A, not_1_out);
  and and_2 (and_2_out, B, Sel);
  or or_1 (Out, and_1_out, and_2_out);
endmodule

module Dmux (
  input  In,
  input  Sel,
  output A,
  output B
);

  wire not_1_out;

  not not_1 (not_1_out, Sel);
  and and_1 (A, In, not_1_out);
  and and_2 (B, In, Sel);
endmodule

module Dmux_4 (
  input  In,
  input  Sel_1,
  input  Sel_0,
  output Out,
  output Out_2,
  output Out_3,
  output Out_4
);

  wire not_1_out, not_2_out, not_3_out, not_4_out;

  not not_1 (not_1_out, Sel_1);
  not not_2 (not_2_out, Sel_0);
  not not_3 (not_3_out, Sel_1);
  not not_4 (not_4_out, Sel_0);
  and and_1 (Out, In, not_1_out, not_2_out);
  and and_2 (Out_2, In, not_3_out, Sel_0);
  and and_3 (Out_3, In, Sel_1, not_4_out);
  and and_4 (Out_4, In, Sel_1, Sel_0);
endmodule

module Mux16 (
  input  Sel,
  input  [15:0] A,
  input  [15:0] B,
  output [15:0] out_4
);

  Mux mux_1 (.A(A[0]), .B(B[0]), .Sel(Sel), .Out(out_4[0]));
  Mux mux_2 (.A(A[1]), .B(B[1]), .Sel(Sel), .Out(out_4[1]));
  Mux mux_3 (.A(A[2]), .B(B[2]), .Sel(Sel), .Out(out_4[2]));
  Mux mux_4 (.A(A[3]), .B(B[3]), .Sel(Sel), .Out(out_4[3]));
  Mux mux_5 (.A(A[4]), .B(B[4]), .Sel(Sel), .Out(out_4[4]));
  Mux mux_6 (.A(A[5]), .B(B[5]), .Sel(Sel), .Out(out_4[5]));
  Mux mux_7 (.A(A[6]), .B(B[6]), .Sel(Sel), .Out(out_4[6]));
  Mux mux_8 (.A(A[7]), .B(B[7]), .Sel(Sel), .Out(out_4[7]));
  Mux mux_9 (.A(A[8]), .B(B[8]), .Sel(Sel), .Out(out_4[8]));
  Mux mux_10 (.A(A[9]), .B(B[9]), .Sel(Sel), .Out(out_4[9]));
  Mux mux_11 (.A(A[10]), .B(B[10]), .Sel(Sel), .Out(out_4[10]));
  Mux mux_12 (.A(A[11]), .B(B[11]), .Sel(Sel), .Out(out_4[11]));
  Mux mux_13 (.A(A[12]), .B(B[12]), .Sel(Sel), .Out(out_4[12]));
  Mux mux_14 (.A(A[13]), .B(B[13]), .Sel(Sel), .Out(out_4[13]));
  Mux mux_15 (.A(A[14]), .B(B[14]), .Sel(Sel), .Out(out_4[14]));
  Mux mux_16 (.A(A[15]), .B(B[15]), .Sel(Sel), .Out(out_4[15]));
endmodule

module OR_16_1 (
  input  [15:0] in_1,
  output out
);

  wire or_1_out, or_2_out, or_3_out, or_4_out, or_5_out, or_6_out, or_7_out, or_8_out, or_9_out, or_10_out,
       or_11_out, or_12_out, or_13_out, or_14_out;

  or or_1 (or_1_out, in_1[0], in_1[1]);
  or or_2 (or_2_out, in_1[2], in_1[3]);
  or or_3 (or_3_out, in_1[4], in_1[5]);
  or or_4 (or_4_out, in_1[6], in_1[7]);
  or or_5 (or_5_out, in_1[8], in_1[9]);
  or or_6 (or_6_out, in_1[10], in_1[11]);
  or or_7 (or_7_out, in_1[12], in_1[13]);
  or or_8 (or_8_out, in_1[14], in_1[15]);
  or or_9 (or_9_out, or_1_out, or_2_out);
  or or_10 (or_10_out, or_3_out, or_4_out);
  or or_11 (or_11_out, or_5_out, or_6_out);
  or or_12 (or_12_out, or_7_out, or_8_out);
  or or_13 (or_13_out, or_9_out, or_10_out);
  or or_14 (or_14_out, or_11_out, or_12_out);
  or or_15 (out, or_13_out, or_14_out);
endmodule

module SR_latch (
  input  Set,
  input  Reset,
  output out_3
);

  wire not_1_out, or_1_out;

  or or_1 (or_1_out, out_3, Set);
  not not_1 (not_1_out, Reset);
  and and_1 (out_3, or_1_out, not_1_out);
endmodule

module SR_Latch__Nor (
  input  Set,
  input  Reset,
  output Out
);

  wire nor_1_out;

  nor nor_1 (nor_1_out, Set, Out);
  nor nor_2 (Out, nor_1_out, Reset);
endmodule

module D_latch (
  input  Data,
  input  Store,
  output Out
);

  wire and_1_out, and_2_out, nor_1_out, not_1_out;

  not not_1 (not_1_out, Data);
  and and_1 (and_1_out, Data, Store);
  and and_2 (and_2_out, Store, not_1_out);
  nor nor_1 (nor_1_out, and_1_out, Out);
  nor nor_2 (Out, nor_1_out, and_2_out);
endmodule

module Register_4_bit (
  input  Data_3,
  input  Data_2,
  input  Data_1,
  input  Data_0,
  input  Store,
  output out_6,
  output out_7,
  output out_8,
  output out_9
);

  D_latch d_latch_1 (.Data(Data_3), .Store(Store), .Out(out_6));
  D_latch d_latch_2 (.Data(Data_2), .Store(Store), .Out(out_7));
  D_latch d_latch_3 (.Data(Data_1), .Store(Store), .Out(out_8));
  D_latch d_latch_4 (.Data(Data_0), .Store(Store), .Out(out_9));

  // Notes on the sheet:
  //   To get around this, you can use a D-flip flop to synchronously store and update values as seen in the 1-Bit Register Chip.
  //   As explained by sebastian lague, this register is faulty. This is because it only uses D-latches for each 1 bit register (that dont have any control over when to store data and constantly store it when the store signal is high)
endmodule

module Register_16_bit (
  input  Data_0,
  input  Data_0_2,
  input  Data_0_3,
  input  Data_0_4,
  input  Data_0_5,
  input  Data_0_6,
  input  Data_0_7,
  input  Data_0_8,
  input  Data_0_9,
  input  Data_0_10,
  input  Data_0_11,
  input  Data_0_12,
  input  Data_0_13,
  input  Data_0_14,
  input  Data_0_15,
  input  Data_0_16,
  input  Store,
  output [15:0] out_18
);

  Register_4_bit register_4_bit_1 (
    .Data_3(Data_0), .Data_2(Data_0_2), .Data_1(Data_0_3), .Data_0(Data_0_4), .Store(Store),
    .out_6(out_18[0]), .out_7(out_18[1]), .out_8(out_18[2]), .out_9(out_18[3]));
  Register_4_bit register_4_bit_2 (
    .Data_3(Data_0_5), .Data_2(Data_0_6), .Data_1(Data_0_7), .Data_0(Data_0_8), .Store(Store),
    .out_6(out_18[4]), .out_7(out_18[5]), .out_8(out_18[6]), .out_9(out_18[7]));
  Register_4_bit register_4_bit_3 (
    .Data_3(Data_0_9), .Data_2(Data_0_10), .Data_1(Data_0_11), .Data_0(Data_0_12), .Store(Store),
    .out_6(out_18[8]), .out_7(out_18[9]), .out_8(out_18[10]), .out_9(out_18[11]));
  Register_4_bit register_4_bit_4 (
    .Data_3(Data_0_13), .Data_2(Data_0_14), .Data_1(Data_0_15), .Data_0(Data_0_16), .Store(Store),
    .out_6(out_18[12]), .out_7(out_18[13]), .out_8(out_18[14]), .out_9(out_18[15]));
endmodule

module D_Flip_Flop (
  input  Data,
  input  Clock,
  output out_3
);

  wire d_latch_1_out, not_1_out;

  D_latch d_latch_1 (.Data(Data), .Store(not_1_out), .Out(d_latch_1_out));
  not not_1 (not_1_out, Clock);
  D_latch d_latch_2 (.Data(d_latch_1_out), .Store(Clock), .Out(out_3));

  // Notes on the sheet:
  //   First latch stores data when clock signal is low.
  //   Second latch copies and outputs data only when the clock signal is high
  //   This is an edge-triggered flip flop (when the clock signal is high, data is stored (and output) [in the second latch]; when the clock signal is low, data can be modified (w/o being stored or modifying the contents of the second latch))
endmodule

module _1_Bit_Register (
  input  Data,
  input  Store,
  input  Clock,
  output out_4
);

  wire mux_1_out;

  Mux mux_1 (.A(out_4), .B(Data), .Sel(Store), .Out(mux_1_out));
  D_Flip_Flop d_flip_flop_1 (.Data(mux_1_out), .Clock(Clock), .out_3(out_4));

  // Notes on the sheet:
  //   and the already stored data and incoming data as inputs to only store new data when the store signal is high.
  //   This 1-Bit register is an improvement over a register made with just a D-latch or a D-flip flop because there is a control over when data is stored (and the value of the stored data isnt changed/updated on every clock tick) via the store input.
  //   A simple way to handle the store signal would be to pass the store and clock signal into an and gate and input that into the store signal of the D-Flip Flop (However, the defect with this would be that the Flip flop wouldnt be able to obtain
  //   the clock reading through the AND gate, and if the store signal comes on while the clock signal is high, data will be stored at the wrong moment). So, to get around this you can use a multiplexer with the store signal as the control wire input
endmodule

module _16_Bit_Register (
  input  Data,
  input  Data_2,
  input  Data_3,
  input  Data_4,
  input  Data_5,
  input  Data_6,
  input  Data_7,
  input  Data_8,
  input  Data_9,
  input  Data_10,
  input  Data_11,
  input  Data_12,
  input  Data_13,
  input  Data_14,
  input  Data_15,
  input  Data_16,
  input  Store,
  input  Clock,
  output [15:0] out_19
);

  _1_Bit_Register u_1_bit_register_1 (.Data(Data), .Store(Store), .Clock(Clock), .out_4(out_19[0]));
  _1_Bit_Register u_1_bit_register_2 (.Data(Data_2), .Store(Store), .Clock(Clock), .out_4(out_19[1]));
  _1_Bit_Register u_1_bit_register_3 (.Data(Data_3), .Store(Store), .Clock(Clock), .out_4(out_19[2]));
  _1_Bit_Register u_1_bit_register_4 (.Data(Data_4), .Store(Store), .Clock(Clock), .out_4(out_19[3]));
  _1_Bit_Register u_1_bit_register_5 (.Data(Data_5), .Store(Store), .Clock(Clock), .out_4(out_19[4]));
  _1_Bit_Register u_1_bit_register_6 (.Data(Data_6), .Store(Store), .Clock(Clock), .out_4(out_19[5]));
  _1_Bit_Register u_1_bit_register_7 (.Data(Data_7), .Store(Store), .Clock(Clock), .out_4(out_19[6]));
  _1_Bit_Register u_1_bit_register_8 (.Data(Data_8), .Store(Store), .Clock(Clock), .out_4(out_19[7]));
  _1_Bit_Register u_1_bit_register_9 (.Data(Data_9), .Store(Store), .Clock(Clock), .out_4(out_19[8]));
  _1_Bit_Register u_1_bit_register_10 (.Data(Data_10), .Store(Store), .Clock(Clock), .out_4(out_19[9]));
  _1_Bit_Register u_1_bit_register_11 (.Data(Data_11), .Store(Store), .Clock(Clock), .out_4(out_19[10]));
  _1_Bit_Register u_1_bit_register_12 (.Data(Data_12), .Store(Store), .Clock(Clock), .out_4(out_19[11]));
  _1_Bit_Register u_1_bit_register_13 (.Data(Data_13), .Store(Store), .Clock(Clock), .out_4(out_19[12]));
  _1_Bit_Register u_1_bit_register_14 (.Data(Data_14), .Store(Store), .Clock(Clock), .out_4(out_19[13]));
  _1_Bit_Register u_1_bit_register_15 (.Data(Data_15), .Store(Store), .Clock(Clock), .out_4(out_19[14]));
  _1_Bit_Register u_1_bit_register_16 (.Data(Data_16), .Store(Store), .Clock(Clock), .out_4(out_19[15]));
endmodule

module Ram_8_Register__16_bit (
  input  [15:0] Data,
  input  [2:0] Address,
  input  Store,
  input  Clock,
  output [15:0] Out
);

  wire and_1_out, and_2_out, dmux_4_1_out, dmux_4_1_out_2, dmux_4_1_out_3, dmux_4_1_out_4, dmux_4_2_out,
       dmux_4_2_out_2, dmux_4_2_out_3, dmux_4_2_out_4, not_1_out;
  wire [15:0] n16_bit_register_simple_1_out, n16_bit_register_simple_2_out, n16_bit_register_simple_3_out,
       n16_bit_register_simple_4_out, n16_bit_register_simple_5_out, n16_bit_register_simple_6_out,
       n16_bit_register_simple_7_out, n16_bit_register_simple_8_out;

  and and_1 (and_1_out, not_1_out, Store);
  not not_1 (not_1_out, Address[2]);
  Dmux_4 dmux_4_1 (
    .In(and_1_out), .Sel_1(Address[1]), .Sel_0(Address[0]), .Out(dmux_4_1_out), .Out_2(dmux_4_1_out_2),
    .Out_3(dmux_4_1_out_3), .Out_4(dmux_4_1_out_4));
  and and_2 (and_2_out, Address[2], Store);
  Dmux_4 dmux_4_2 (
    .In(and_2_out), .Sel_1(Address[1]), .Sel_0(Address[0]), .Out(dmux_4_2_out), .Out_2(dmux_4_2_out_2),
    .Out_3(dmux_4_2_out_3), .Out_4(dmux_4_2_out_4));
  _16_Bit_Register_simple u_16_bit_register_simple_1 (
    .A(Data), .Store(dmux_4_1_out), .Clock(Clock), .Out(n16_bit_register_simple_1_out));
  _16_Bit_Register_simple u_16_bit_register_simple_2 (
    .A(Data), .Store(dmux_4_1_out_2), .Clock(Clock), .Out(n16_bit_register_simple_2_out));
  _16_Bit_Register_simple u_16_bit_register_simple_3 (
    .A(Data), .Store(dmux_4_1_out_3), .Clock(Clock), .Out(n16_bit_register_simple_3_out));
  _16_Bit_Register_simple u_16_bit_register_simple_4 (
    .A(Data), .Store(dmux_4_1_out_4), .Clock(Clock), .Out(n16_bit_register_simple_4_out));
  _16_Bit_Register_simple u_16_bit_register_simple_5 (
    .A(Data), .Store(dmux_4_2_out), .Clock(Clock), .Out(n16_bit_register_simple_5_out));
  _16_Bit_Register_simple u_16_bit_register_simple_6 (
    .A(Data), .Store(dmux_4_2_out_2), .Clock(Clock), .Out(n16_bit_register_simple_6_out));
  _16_Bit_Register_simple u_16_bit_register_simple_7 (
    .A(Data), .Store(dmux_4_2_out_3), .Clock(Clock), .Out(n16_bit_register_simple_7_out));
  _16_Bit_Register_simple u_16_bit_register_simple_8 (
    .A(Data), .Store(dmux_4_2_out_4), .Clock(Clock), .Out(n16_bit_register_simple_8_out));
  Ram_Output_Selector ram_output_selector_1 (
    ._0(n16_bit_register_simple_1_out), ._1(n16_bit_register_simple_2_out),
    ._2(n16_bit_register_simple_3_out), ._3(n16_bit_register_simple_4_out),
    ._4(n16_bit_register_simple_5_out), ._5(n16_bit_register_simple_6_out),
    ._6(n16_bit_register_simple_7_out), ._7(n16_bit_register_simple_8_out), .Address(Address), .out(Out));

  // Notes on the sheet:
  //   Note: Instead of a DMUX(8), I used 2 DMUX(4)s and AND gate logic combined w/ the last address bit to choose which DMUX(4) to use to create the behaviour of a DMUX(8). 
  //   To route the store signal to the correct register, so the correct data is stored, you have to make a Dmux(8) gate, and then use a Mux(8) gate to send the correct register output to the output pin based off of the same address input
  //   The store and address signals are AND together (so the store bit of the register denoted by the address input is only HIGH when STORE is HIGH) and the correct address to output the store signal to is chosen via DMUX logic. 
endmodule

module _16_Bit_Register_simple (
  input  [15:0] A,
  input  Store,
  input  Clock,
  output [15:0] Out
);

  _16_Bit_Register u_16_bit_register_1 (
    .Data(A[0]), .Data_2(A[1]), .Data_3(A[2]), .Data_4(A[3]), .Data_5(A[4]), .Data_6(A[5]), .Data_7(A[6]),
    .Data_8(A[7]), .Data_9(A[8]), .Data_10(A[9]), .Data_11(A[10]), .Data_12(A[11]), .Data_13(A[12]),
    .Data_14(A[13]), .Data_15(A[14]), .Data_16(A[15]), .Store(Store), .Clock(Clock), .out_19(Out));
endmodule

module Ram_Output_Selector (
  input  [15:0] _0,
  input  [15:0] _1,
  input  [15:0] _2,
  input  [15:0] _3,
  input  [15:0] _4,
  input  [15:0] _5,
  input  [15:0] _6,
  input  [15:0] _7,
  input  [2:0] Address,
  output [15:0] out
);

  wire and_1_out, and_2_out, and_3_out, and_4_out, and_5_out, and_6_out, and_7_out, and_8_out, not_1_out,
       not_2_out, not_3_out, not_4_out, not_5_out, not_6_out, not_7_out, not_8_out, not_9_out, not_10_out,
       not_11_out, not_12_out;
  wire [15:0] mux16_1_out_4, mux16_2_out_4, mux16_3_out_4, mux16_4_out_4, mux16_5_out_4, mux16_6_out_4,
       mux16_7_out_4, mux16_8_out_4, or16_1_out, or16_2_out, or16_3_out, or16_4_out, or16_5_out, or16_6_out;

  not not_1 (not_1_out, Address[0]);
  not not_2 (not_2_out, Address[1]);
  Mux16 mux16_1 (.A({16{1'b0}}), .B(_0), .Sel(and_1_out), .out_4(mux16_1_out_4));
  and and_1 (and_1_out, not_1_out, not_2_out, not_3_out);
  not not_3 (not_3_out, Address[2]);
  and and_2 (and_2_out, Address[0], not_4_out, not_5_out);
  not not_4 (not_4_out, Address[1]);
  not not_5 (not_5_out, Address[2]);
  Mux16 mux16_2 (.A({16{1'b0}}), .B(_1), .Sel(and_2_out), .out_4(mux16_2_out_4));
  not not_6 (not_6_out, Address[2]);
  not not_7 (not_7_out, Address[0]);
  OR16 or16_1 (.A(mux16_1_out_4), .B(mux16_2_out_4), .Out(or16_1_out));
  and and_3 (and_3_out, not_7_out, Address[1], not_6_out);
  not not_8 (not_8_out, Address[2]);
  Mux16 mux16_3 (.A({16{1'b0}}), .B(_2), .Sel(and_3_out), .out_4(mux16_3_out_4));
  and and_4 (and_4_out, Address[0], Address[1], not_8_out);
  not not_9 (not_9_out, Address[1]);
  not not_10 (not_10_out, Address[0]);
  OR16 or16_2 (.A(or16_1_out), .B(mux16_3_out_4), .Out(or16_2_out));
  and and_5 (and_5_out, not_10_out, not_9_out, Address[2]);
  not not_11 (not_11_out, Address[1]);
  Mux16 mux16_4 (.A({16{1'b0}}), .B(_3), .Sel(and_4_out), .out_4(mux16_4_out_4));
  and and_6 (and_6_out, Address[0], not_11_out, Address[2]);
  not not_12 (not_12_out, Address[0]);
  OR16 or16_3 (.A(or16_2_out), .B(mux16_4_out_4), .Out(or16_3_out));
  and and_7 (and_7_out, not_12_out, Address[1], Address[2]);
  Mux16 mux16_5 (.A({16{1'b0}}), .B(_4), .Sel(and_5_out), .out_4(mux16_5_out_4));
  and and_8 (and_8_out, Address[0], Address[1], Address[2]);
  OR16 or16_4 (.A(or16_3_out), .B(mux16_5_out_4), .Out(or16_4_out));
  Mux16 mux16_6 (.A({16{1'b0}}), .B(_5), .Sel(and_6_out), .out_4(mux16_6_out_4));
  OR16 or16_5 (.A(or16_4_out), .B(mux16_6_out_4), .Out(or16_5_out));
  Mux16 mux16_7 (.A({16{1'b0}}), .B(_6), .Sel(and_7_out), .out_4(mux16_7_out_4));
  OR16 or16_6 (.A(or16_5_out), .B(mux16_7_out_4), .Out(or16_6_out));
  OR16 or16_7 (.A(or16_6_out), .B(mux16_8_out_4), .Out(out));
  Mux16 mux16_8 (.A({16{1'b0}}), .B(_7), .Sel(and_8_out), .out_4(mux16_8_out_4));
endmodule

module Ram_64_register__16_bit (
  input  [15:0] Data,
  input  [5:0] Address,
  input  Store,
  input  Clock,
  output [15:0] out_5
);

  wire [15:0] ram_8_register_16_bit_1_out, ram_8_register_16_bit_2_out, ram_8_register_16_bit_3_out,
       ram_8_register_16_bit_4_out, ram_8_register_16_bit_5_out, ram_8_register_16_bit_6_out,
       ram_8_register_16_bit_7_out, ram_8_register_16_bit_8_out;

  Ram_8_Register__16_bit ram_8_register_16_bit_1 (
    .Data(Data), .Store(Store), .Clock(Clock), .Out(ram_8_register_16_bit_1_out));  // open: Address
  Ram_8_Register__16_bit ram_8_register_16_bit_2 (
    .Data(Data), .Store(Store), .Clock(Clock), .Out(ram_8_register_16_bit_2_out));  // open: Address
  Ram_8_Register__16_bit ram_8_register_16_bit_3 (
    .Data(Data), .Store(Store), .Clock(Clock), .Out(ram_8_register_16_bit_3_out));  // open: Address
  Ram_8_Register__16_bit ram_8_register_16_bit_4 (
    .Data(Data), .Store(Store), .Clock(Clock), .Out(ram_8_register_16_bit_4_out));  // open: Address
  Ram_8_Register__16_bit ram_8_register_16_bit_5 (
    .Data(Data), .Store(Store), .Clock(Clock), .Out(ram_8_register_16_bit_5_out));  // open: Address
  Ram_8_Register__16_bit ram_8_register_16_bit_6 (
    .Data(Data), .Store(Store), .Clock(Clock), .Out(ram_8_register_16_bit_6_out));  // open: Address
  Ram_8_Register__16_bit ram_8_register_16_bit_7 (
    .Data(Data), .Store(Store), .Clock(Clock), .Out(ram_8_register_16_bit_7_out));  // open: Address
  Ram_8_Register__16_bit ram_8_register_16_bit_8 (
    .Data(Data), .Store(Store), .Clock(Clock), .Out(ram_8_register_16_bit_8_out));  // open: Address
  assign out_5 = ram_8_register_16_bit_1_out | ram_8_register_16_bit_2_out | ram_8_register_16_bit_3_out | ram_8_register_16_bit_4_out | ram_8_register_16_bit_5_out | ram_8_register_16_bit_6_out | ram_8_register_16_bit_7_out | ram_8_register_16_bit_8_out;  // OR_Gate or_1, 16 bits wide
endmodule

module Program_Counter__16_Bit (
  input  Increment,
  input  Reset,
  input  Load,
  input  [15:0] Set,
  input  Clock,
  output [15:0] Out
);

  wire and_1_out, and_2_out, not_1_out, not_2_out, or_1_out;
  wire [15:0] controlled_buffer_1_out, mux16_1_out_4, n16_bit_adder_1_out;

  not not_1 (not_1_out, Reset);
  not not_2 (not_2_out, Load);
  and and_1 (and_1_out, Reset, not_2_out);
  and and_2 (and_2_out, not_1_out, Load);
  assign controlled_buffer_1_out = and_2_out ? Set : 16'bz;  // Controlled_Buffer controlled_buffer_1
  assign controlled_buffer_1_out = and_1_out ? {16{1'b0}} : 16'bz;  // Controlled_Buffer controlled_buffer_2
  or or_1 (or_1_out, Increment, Reset, Load);
  _16_bit_adder u_16_bit_adder_1 (.A(Out), .B(16'h1), .Out(n16_bit_adder_1_out));
  Mux16 mux16_1 (.A(controlled_buffer_1_out), .B(n16_bit_adder_1_out), .Sel(Increment), .out_4(mux16_1_out_4));
  _16_Bit_Register_simple u_16_bit_register_simple_1 (.A(mux16_1_out_4), .Store(or_1_out), .Clock(Clock), .Out(Out));
endmodule
