// Logisim project adders_NAND.circ as structural Verilog: 6 circuits, main circuit Half Adder
module Half_Adder (
  input  A,
  input  B,
  output Sum,
  output carry
);

  xor xor_1 (Sum, A, B);
  and and_1 (carry, B, A);
endmodule

module Full_Adder (
  input  c,
  input  A,
  input  B,
  output Sum,
  output Carry
);

  wire and_1_out, and_2_out, and_3_out, and_4_out, and_5_out, and_6_out, and_7_out, not_1_out, not_2_out,
       not_3_out, not_4_out, not_5_out, not_6_out;

  not not_1 (not_1_out, c);
  not not_2 (not_2_out, A);
  not not_3 (not_3_out, c);
  not not_4 (not_4_out, B);
  not not_5 (not_5_out, A);
  not not_6 (not_6_out, B);
  and and_1 (and_1_out, A, B);
  and and_2 (and_2_out, c, B);
  and and_3 (and_3_out, c, A);
  and and_4 (and_4_out, not_1_out, not_2_out, B);
  and and_5 (and_5_out, not_3_out, A, not_4_out);
  and and_6 (and_6_out, c, not_5_out, not_6_out);
  and and_7 (and_7_out, c, A, B);
  or or_1 (Carry, and_1_out, and_2_out, and_3_out);
  or or_2 (Sum, and_4_out, and_5_out, and_6_out, and_7_out);
endmodule

module Full_Adder_alternate (
  input  c,
  input  A,
  input  B,
  output Sum,
  output Carry
);

  wire and_1_out, and_2_out, and_3_out, xor_1_out, xor_2_out;

  xor xor_1 (xor_1_out, A, B);
  xor xor_2 (xor_2_out, c, xor_1_out);
  and and_1 (and_1_out, B, A);
  and and_2 (and_2_out, xor_1_out, c);
  and and_3 (and_3_out, c, and_1_out);
  or or_1 (Carry, and_1_out, and_2_out);
  or or_2 (Sum, xor_2_out, and_3_out);
endmodule

module _8_Bit_Adder (
  input  [7:0] A,
  input  [7:0] B,
  output [7:0] Out
);

  wire full_adder_1_carry, full_adder_2_carry, full_adder_3_carry, full_adder_4_carry, full_adder_5_carry,
       full_adder_6_carry, half_adder_1_carry;

  Half_Adder half_adder_1 (.A(A[0]), .B(B[0]), .Sum(Out[0]), .carry(half_adder_1_carry));
  Full_Adder full_adder_1 (.c(half_adder_1_carry), .A(A[1]), .B(B[1]), .Sum(Out[1]), .Carry(full_adder_1_carry));
  Full_Adder full_adder_2 (.c(full_adder_1_carry), .A(A[2]), .B(B[2]), .Sum(Out[2]), .Carry(full_adder_2_carry));
  Full_Adder full_adder_3 (.c(full_adder_2_carry), .A(A[3]), .B(B[3]), .Sum(Out[3]), .Carry(full_adder_3_carry));
  Full_Adder full_adder_4 (.c(full_adder_3_carry), .A(A[4]), .B(B[4]), .Sum(Out[4]), .Carry(full_adder_4_carry));
  Full_Adder full_adder_5 (.c(full_adder_4_carry), .A(A[5]), .B(B[5]), .Sum(Out[5]), .Carry(full_adder_5_carry));
  Full_Adder full_adder_6 (.c(full_adder_5_carry), .A(A[6]), .B(B[6]), .Sum(Out[6]), .Carry(full_adder_6_carry));
  Full_Adder full_adder_7 (.c(full_adder_6_carry), .A(A[7]), .B(B[7]), .Sum(Out[7]));  // open: Carry
endmodule

module _16_Bit_Adder (
  input  [15:0] A,
  input  [15:0] B,
  output [15:0] Out
);

  wire full_adder_1_carry, full_adder_2_carry, full_adder_3_carry, full_adder_4_carry, full_adder_5_carry,
       full_adder_6_carry, full_adder_7_carry, full_adder_8_carry, full_adder_9_carry, full_adder_10_carry,
       full_adder_11_carry, full_adder_12_carry, full_adder_13_carry, full_adder_14_carry, half_adder_1_carry;

  Half_Adder half_adder_1 (.A(A[0]), .B(B[0]), .Sum(Out[0]), .carry(half_adder_1_carry));
  Full_Adder full_adder_1 (.c(half_adder_1_carry), .A(A[1]), .B(B[1]), .Sum(Out[1]), .Carry(full_adder_1_carry));
  Full_Adder full_adder_2 (.c(full_adder_1_carry), .A(A[2]), .B(B[2]), .Sum(Out[2]), .Carry(full_adder_2_carry));
  Full_Adder full_adder_3 (.c(full_adder_2_carry), .A(A[3]), .B(B[3]), .Sum(Out[3]), .Carry(full_adder_3_carry));
  Full_Adder full_adder_4 (.c(full_adder_3_carry), .A(A[4]), .B(B[4]), .Sum(Out[4]), .Carry(full_adder_4_carry));
  Full_Adder full_adder_5 (.c(full_adder_4_carry), .A(A[5]), .B(B[5]), .Sum(Out[5]), .Carry(full_adder_5_carry));
  Full_Adder full_adder_6 (.c(full_adder_5_carry), .A(A[6]), .B(B[6]), .Sum(Out[6]), .Carry(full_adder_6_carry));
  Full_Adder full_adder_7 (.c(full_adder_6_carry), .A(A[7]), .B(B[7]), .Sum(Out[7]), .Carry(full_adder_7_carry));
  Full_Adder full_adder_8 (.c(full_adder_7_carry), .A(A[8]), .B(B[8]), .Sum(Out[8]), .Carry(full_adder_8_carry));
  Full_Adder full_adder_9 (.c(full_adder_8_carry), .A(A[9]), .B(B[9]), .Sum(Out[9]), .Carry(full_adder_9_carry));
  Full_Adder full_adder_10 (.c(full_adder_9_carry), .A(A[10]), .B(B[10]), .Sum(Out[10]), .Carry(full_adder_10_carry));
  Full_Adder full_adder_11 (.c(full_adder_10_carry), .A(A[11]), .B(B[11]), .Sum(Out[11]), .Carry(full_adder_11_carry));
  Full_Adder full_adder_12 (.c(full_adder_11_carry), .A(A[12]), .B(B[12]), .Sum(Out[12]), .Carry(full_adder_12_carry));
  Full_Adder full_adder_13 (.c(full_adder_12_carry), .A(A[13]), .B(B[13]), .Sum(Out[13]), .Carry(full_adder_13_carry));
  Full_Adder full_adder_14 (.c(full_adder_13_carry), .A(A[14]), .B(B[14]), .Sum(Out[14]), .Carry(full_adder_14_carry));
  Full_Adder full_adder_15 (.c(full_adder_14_carry), .A(A[15]), .B(B[15]), .Sum(Out[15]));  // open: Carry
endmodule

module _16_Bit_Incrementer (
  input  [15:0] A,
  output [15:0] Out
);

  wire full_adder_1_carry, full_adder_2_carry, full_adder_3_carry, full_adder_4_carry, full_adder_5_carry,
       full_adder_6_carry, full_adder_7_carry, full_adder_8_carry, full_adder_9_carry, full_adder_10_carry,
       full_adder_11_carry, full_adder_12_carry, full_adder_13_carry, full_adder_14_carry,
       half_adder_1_carry, not_1_out;

  not not_1 (not_1_out, 1'b1);
  Half_Adder half_adder_1 (.A(A[0]), .B(1'b1), .Sum(Out[0]), .carry(half_adder_1_carry));
  Full_Adder full_adder_1 (.c(half_adder_1_carry), .A(A[1]), .B(not_1_out), .Sum(Out[1]), .Carry(full_adder_1_carry));
  Full_Adder full_adder_2 (.c(full_adder_1_carry), .A(A[2]), .B(not_1_out), .Sum(Out[2]), .Carry(full_adder_2_carry));
  Full_Adder full_adder_3 (.c(full_adder_2_carry), .A(A[3]), .B(not_1_out), .Sum(Out[3]), .Carry(full_adder_3_carry));
  Full_Adder full_adder_4 (.c(full_adder_3_carry), .A(A[4]), .B(not_1_out), .Sum(Out[4]), .Carry(full_adder_4_carry));
  Full_Adder full_adder_5 (.c(full_adder_4_carry), .A(A[5]), .B(not_1_out), .Sum(Out[5]), .Carry(full_adder_5_carry));
  Full_Adder full_adder_6 (.c(full_adder_5_carry), .A(A[6]), .B(not_1_out), .Sum(Out[6]), .Carry(full_adder_6_carry));
  Full_Adder full_adder_7 (.c(full_adder_6_carry), .A(A[7]), .B(not_1_out), .Sum(Out[7]), .Carry(full_adder_7_carry));
  Full_Adder full_adder_8 (.c(full_adder_7_carry), .A(A[8]), .B(not_1_out), .Sum(Out[8]), .Carry(full_adder_8_carry));
  Full_Adder full_adder_9 (.c(full_adder_8_carry), .A(A[9]), .B(not_1_out), .Sum(Out[9]), .Carry(full_adder_9_carry));
  Full_Adder full_adder_10 (
    .c(full_adder_9_carry), .A(A[10]), .B(not_1_out), .Sum(Out[10]), .Carry(full_adder_10_carry));
  Full_Adder full_adder_11 (
    .c(full_adder_10_carry), .A(A[11]), .B(not_1_out), .Sum(Out[11]), .Carry(full_adder_11_carry));
  Full_Adder full_adder_12 (
    .c(full_adder_11_carry), .A(A[12]), .B(not_1_out), .Sum(Out[12]), .Carry(full_adder_12_carry));
  Full_Adder full_adder_13 (
    .c(full_adder_12_carry), .A(A[13]), .B(not_1_out), .Sum(Out[13]), .Carry(full_adder_13_carry));
  Full_Adder full_adder_14 (
    .c(full_adder_13_carry), .A(A[14]), .B(not_1_out), .Sum(Out[14]), .Carry(full_adder_14_carry));
  Full_Adder full_adder_15 (.c(full_adder_14_carry), .A(A[15]), .B(not_1_out), .Sum(Out[15]));  // open: Carry
endmodule
