// Logisim project cpu_NAND.circ as structural Verilog: 2 circuits, main circuit ALU
module ALU (
  input  ZX,
  input  NX,
  input  ZY,
  input  NY,
  input  F,
  input  NO,
  input  [15:0] A,
  input  [15:0] B,
  output [15:0] out_9,
  output ZR,
  output NG
);

  wire or_1_out;
  wire [15:0] AND16_out, Mux16_2_out_4, Mux16_3_out_4, Mux16_4_out_4, Mux16_5_out_4, Mux16_out_4,
       n16_bit_adder_1_out, not_1_out, not_2_out, not_3_out, not_4_out, not_5_out;

  assign not_1_out = ~{16{1'b1}};  // NOT_Gate not_1, 16 bits wide
  Mux16 Mux16 (.A(A), .B(not_1_out), .Sel(ZX), .out_4(Mux16_out_4));
  Mux16 Mux16_2 (.A(Mux16_out_4), .B(not_2_out), .Sel(NX), .out_4(Mux16_2_out_4));
  assign not_2_out = ~Mux16_out_4;  // NOT_Gate not_2, 16 bits wide
  assign not_3_out = ~{16{1'b1}};  // NOT_Gate not_3, 16 bits wide
  Mux16 Mux16_3 (.A(B), .B(not_3_out), .Sel(ZY), .out_4(Mux16_3_out_4));
  assign not_4_out = ~Mux16_3_out_4;  // NOT_Gate not_4, 16 bits wide
  Mux16 Mux16_4 (.A(Mux16_3_out_4), .B(not_4_out), .Sel(NY), .out_4(Mux16_4_out_4));
  _16_Bit_Adder u_16_bit_adder_1 (.A(Mux16_2_out_4), .B(Mux16_4_out_4), .Out(n16_bit_adder_1_out));
  AND16 AND16 (.A(Mux16_2_out_4), .B(Mux16_4_out_4), .Out(AND16_out));
  Mux16 Mux16_5 (.A(AND16_out), .B(n16_bit_adder_1_out), .Sel(F), .out_4(Mux16_5_out_4));
  assign not_5_out = ~Mux16_5_out_4;  // NOT_Gate not_5, 16 bits wide
  not not_6 (ZR, or_1_out);
  Mux16 Mux16_6 (.A(Mux16_5_out_4), .B(not_5_out), .Sel(NO), .out_4({NG, out_9[14:0]}));
  or or_1 (or_1_out, NG, out_9[14], out_9[13], out_9[12], out_9[11], out_9[10], out_9[9], out_9[8], out_9[7], out_9[6], out_9[5], out_9[4], out_9[3], out_9[2], out_9[1], out_9[0]);

  assign out_9[15] = NG;
endmodule

module PC (
  input  Increment,
  input  Reset,
  input  Load,
  input  [15:0] Set,
  input  Clock,
  output [15:0] Out
);

  wire and_1_out, and_2_out, not_1_out, not_2_out, or_1_out;
  wire [15:0] controlled_buffer_1_out, mux16_1_out_4, n16_bit_adder_1_out;

  not not_1 (not_1_out, Reset);
  not not_2 (not_2_out, Load);
  and and_1 (and_1_out, Reset, not_2_out);
  and and_2 (and_2_out, not_1_out, Load);
  assign controlled_buffer_1_out = and_2_out ? Set : 16'bz;  // Controlled_Buffer controlled_buffer_1
  assign controlled_buffer_1_out = and_1_out ? {16{1'b0}} : 16'bz;  // Controlled_Buffer controlled_buffer_2
  or or_1 (or_1_out, Increment, Reset, Load);
  _16_Bit_Adder u_16_bit_adder_1 (.A(Out), .B(16'h1), .Out(n16_bit_adder_1_out));
  Mux16 mux16_1 (.A(controlled_buffer_1_out), .B(n16_bit_adder_1_out), .Sel(Increment), .out_4(mux16_1_out_4));
  _16_Bit_Register u_16_bit_register_1 (.Data(mux16_1_out_4), .Store(or_1_out), .Clock(Clock), .out_4(Out));
endmodule
