// Logisim project gates_NAND.circ as structural Verilog: 7 circuits, main circuit AND16
module AND16 (
  input  [15:0] A,
  input  [15:0] B,
  output [15:0] Out
);

  and and_1 (Out[0], A[0], B[0]);
  and and_2 (Out[1], A[1], B[1]);
  and and_3 (Out[2], A[2], B[2]);
  and and_4 (Out[3], A[3], B[3]);
  and and_5 (Out[4], A[4], B[4]);
  and and_6 (Out[5], A[5], B[5]);
  and and_7 (Out[6], A[6], B[6]);
  and and_8 (Out[7], A[7], B[7]);
  and and_9 (Out[8], A[8], B[8]);
  and and_10 (Out[9], A[9], B[9]);
  and and_11 (Out[10], A[10], B[10]);
  and and_12 (Out[11], A[11], B[11]);
  and and_13 (Out[12], A[12], B[12]);
  and and_14 (Out[13], A[13], B[13]);
  and and_15 (Out[14], A[14], B[14]);
  and and_16 (Out[15], A[15], B[15]);
endmodule

module OR16 (
  input  [15:0] A,
  input  [15:0] B,
  output [15:0] Out
);

  or or_1 (Out[0], A[0], B[0]);
  or or_2 (Out[1], A[1], B[1]);
  or or_3 (Out[2], A[2], B[2]);
  or or_4 (Out[3], A[3], B[3]);
  or or_5 (Out[4], A[4], B[4]);
  or or_6 (Out[5], A[5], B[5]);
  or or_7 (Out[6], A[6], B[6]);
  or or_8 (Out[7], A[7], B[7]);
  or or_9 (Out[8], A[8], B[8]);
  or or_10 (Out[9], A[9], B[9]);
  or or_11 (Out[10], A[10], B[10]);
  or or_12 (Out[11], A[11], B[11]);
  or or_13 (Out[12], A[12], B[12]);
  or or_14 (Out[13], A[13], B[13]);
  or or_15 (Out[14], A[14], B[14]);
  or or_16 (Out[15], A[15], B[15]);
endmodule

module Mux (
  input  A,
  input  B,
  input  Sel,
  output Out
);

  wire and_1_out, and_2_out, not_1_out;

  not not_1 (not_1_out, Sel);
  and and_1 (and_1_out, A, not_1_out);
  and and_2 (and_2_out, B, Sel);
  or or_1 (Out, and_1_out, and_2_out);
endmodule

module Mux4 (
  input  A,
  input  B,
  input  C,
  input  D,
  input  Sel_0,
  input  Sel_1,
  output Out
);

  wire and_1_out, and_2_out, and_3_out, and_4_out, not_1_out, not_2_out, not_3_out, not_4_out;

  not not_1 (not_1_out, Sel_0);
  not not_2 (not_2_out, Sel_1);
  not not_3 (not_3_out, Sel_0);
  not not_4 (not_4_out, Sel_1);
  and and_1 (and_1_out, A, not_1_out, not_2_out);
  and and_2 (and_2_out, B, not_3_out, Sel_1);
  and and_3 (and_3_out, C, Sel_0, not_4_out);
  and and_4 (and_4_out, D, Sel_0, Sel_1);
  or or_1 (Out, and_1_out, and_2_out, and_3_out, and_4_out);
endmodule

module DMux (
  input  In,
  input  Sel,
  output A,
  output B
);

  wire not_1_out;

  not not_1 (not_1_out, Sel);
  and and_1 (A, In, not_1_out);
  and and_2 (B, In, Sel);
endmodule

module DMux4 (
  input  In,
  input  Sel_1,
  input  Sel_0,
  output Out,
  output Out_2,
  output Out_3,
  output Out_4
);

  wire not_1_out, not_2_out, not_3_out, not_4_out;

  not not_1 (not_1_out, Sel_1);
  not not_2 (not_2_out, Sel_0);
  not not_3 (not_3_out, Sel_1);
  not not_4 (not_4_out, Sel_0);
  and and_1 (Out, In, not_1_out, not_2_out);
  and and_2 (Out_2, In, not_3_out, Sel_0);
  and and_3 (Out_3, In, Sel_1, not_4_out);
  and and_4 (Out_4, In, Sel_1, Sel_0);
endmodule

module Mux16 (
  input  Sel,
  input  [15:0] A,
  input  [15:0] B,
  output [15:0] out_4
);

  Mux mux_1 (.A(A[0]), .B(B[0]), .Sel(Sel), .Out(out_4[0]));
  Mux mux_2 (.A(A[1]), .B(B[1]), .Sel(Sel), .Out(out_4[1]));
  Mux mux_3 (.A(A[2]), .B(B[2]), .Sel(Sel), .Out(out_4[2]));
  Mux mux_4 (.A(A[3]), .B(B[3]), .Sel(Sel), .Out(out_4[3]));
  Mux mux_5 (.A(A[4]), .B(B[4]), .Sel(Sel), .Out(out_4[4]));
  Mux mux_6 (.A(A[5]), .B(B[5]), .Sel(Sel), .Out(out_4[5]));
  Mux mux_7 (.A(A[6]), .B(B[6]), .Sel(Sel), .Out(out_4[6]));
  Mux mux_8 (.A(A[7]), .B(B[7]), .Sel(Sel), .Out(out_4[7]));
  Mux mux_9 (.A(A[8]), .B(B[8]), .Sel(Sel), .Out(out_4[8]));
  Mux mux_10 (.A(A[9]), .B(B[9]), .Sel(Sel), .Out(out_4[9]));
  Mux mux_11 (.A(A[10]), .B(B[10]), .Sel(Sel), .Out(out_4[10]));
  Mux mux_12 (.A(A[11]), .B(B[11]), .Sel(Sel), .Out(out_4[11]));
  Mux mux_13 (.A(A[12]), .B(B[12]), .Sel(Sel), .Out(out_4[12]));
  Mux mux_14 (.A(A[13]), .B(B[13]), .Sel(Sel), .Out(out_4[13]));
  Mux mux_15 (.A(A[14]), .B(B[14]), .Sel(Sel), .Out(out_4[14]));
  Mux mux_16 (.A(A[15]), .B(B[15]), .Sel(Sel), .Out(out_4[15]));
endmodule
