// Logisim project memory_NAND.circ as structural Verilog: 13 circuits, main circuit SR Latch
module SR_Latch (
  input  Set,
  input  Reset,
  output Out
);

  wire nor_1_out;

  nor nor_1 (nor_1_out, Set, Out);
  nor nor_2 (Out, nor_1_out, Reset);
endmodule

module SR_Latch__Alt (
  input  Set,
  input  Reset,
  output out_3
);

  wire not_1_out, or_1_out;

  or or_1 (or_1_out, out_3, Set);
  not not_1 (not_1_out, Reset);
  and and_1 (out_3, or_1_out, not_1_out);
endmodule

module D_Latch (
  input  Data,
  input  Store,
  output Out
);

  wire and_1_out, and_2_out, nor_1_out, not_1_out;

  not not_1 (not_1_out, Data);
  and and_1 (and_1_out, Data, Store);
  and and_2 (and_2_out, Store, not_1_out);
  nor nor_1 (nor_1_out, and_1_out, Out);
  nor nor_2 (Out, nor_1_out, and_2_out);
endmodule

module _4_Bit_Register__D_Latch (
  input  Data_3,
  input  Data_2,
  input  Data_1,
  input  Data_0,
  input  Store,
  output out_6,
  output out_7,
  output out_8,
  output out_9
);

  D_Latch d_latch_1 (.Data(Data_3), .Store(Store), .Out(out_6));
  D_Latch d_latch_2 (.Data(Data_2), .Store(Store), .Out(out_7));
  D_Latch d_latch_3 (.Data(Data_1), .Store(Store), .Out(out_8));
  D_Latch d_latch_4 (.Data(Data_0), .Store(Store), .Out(out_9));

  // Notes on the sheet:
  //   To get around this, you can use a D-flip flop to synchronously store and update values as seen in the 1-Bit Register Chip.
  //   As explained by sebastian lague, this register is faulty. This is because it only uses D-latches for each 1 bit register (that dont have any control over when to store data and constantly store it when the store signal is high)
endmodule

module _16_Bit_Register__D_Latch (
  input  Data_0,
  input  Data_0_2,
  input  Data_0_3,
  input  Data_0_4,
  input  Data_0_5,
  input  Data_0_6,
  input  Data_0_7,
  input  Data_0_8,
  input  Data_0_9,
  input  Data_0_10,
  input  Data_0_11,
  input  Data_0_12,
  input  Data_0_13,
  input  Data_0_14,
  input  Data_0_15,
  input  Data_0_16,
  input  Store,
  output [15:0] out_18
);

  _4_Bit_Register__D_Latch u_4_bit_register_d_latch_1 (
    .Data_3(Data_0), .Data_2(Data_0_2), .Data_1(Data_0_3), .Data_0(Data_0_4), .Store(Store),
    .out_6(out_18[0]), .out_7(out_18[1]), .out_8(out_18[2]), .out_9(out_18[3]));
  _4_Bit_Register__D_Latch u_4_bit_register_d_latch_2 (
    .Data_3(Data_0_5), .Data_2(Data_0_6), .Data_1(Data_0_7), .Data_0(Data_0_8), .Store(Store),
    .out_6(out_18[4]), .out_7(out_18[5]), .out_8(out_18[6]), .out_9(out_18[7]));
  _4_Bit_Register__D_Latch u_4_bit_register_d_latch_3 (
    .Data_3(Data_0_9), .Data_2(Data_0_10), .Data_1(Data_0_11), .Data_0(Data_0_12), .Store(Store),
    .out_6(out_18[8]), .out_7(out_18[9]), .out_8(out_18[10]), .out_9(out_18[11]));
  _4_Bit_Register__D_Latch u_4_bit_register_d_latch_4 (
    .Data_3(Data_0_13), .Data_2(Data_0_14), .Data_1(Data_0_15), .Data_0(Data_0_16), .Store(Store),
    .out_6(out_18[12]), .out_7(out_18[13]), .out_8(out_18[14]), .out_9(out_18[15]));

  // Notes on the sheet:
  //   For the same reason the 4-Bit D Latch register is faulty, this one is as well. It has no way of synchronizing data storage.
endmodule

module D_Flip_Flop (
  input  Data,
  input  Clock,
  output out_3
);

  wire d_latch_1_out, not_1_out;

  D_Latch d_latch_1 (.Data(Data), .Store(not_1_out), .Out(d_latch_1_out));
  not not_1 (not_1_out, Clock);
  D_Latch d_latch_2 (.Data(d_latch_1_out), .Store(Clock), .Out(out_3));

  // Notes on the sheet:
  //   First latch stores data when clock signal is low.
  //   Second latch copies and outputs data only when the clock signal is high
  //   This is an edge-triggered flip flop (when the clock signal is high, data is stored (and output) [in the second latch]; when the clock signal is low, data can be modified (w/o being stored or modifying the contents of the second latch))
endmodule

module _1_Bit_Register (
  input  Data,
  input  Store,
  input  Clock,
  output out_4
);

  wire mux_1_out;

  Mux mux_1 (.A(out_4), .B(Data), .Sel(Store), .Out(mux_1_out));
  D_Flip_Flop d_ff_1 (.Data(mux_1_out), .Clock(Clock), .out_3(out_4));

  // Notes on the sheet:
  //   and the already stored data and incoming data as inputs to only store new data when the store signal is high.
  //   This 1-Bit register is an improvement over a register made with just a D-latch or a D-flip flop because there is a control over when data is stored (and the value of the stored data isnt changed/updated on every clock tick) via the store input.
  //   A simple way to handle the store signal would be to pass the store and clock signal into an and gate and input that into the store signal of the D-Flip Flop (However, the defect with this would be that the Flip flop wouldnt be able to obtain
  //   the clock reading through the AND gate, and if the store signal comes on while the clock signal is high, data will be stored at the wrong moment). So, to get around this you can use a multiplexer with the store signal as the control wire input
endmodule

module _16_Bit_Register (
  input  [15:0] Data,
  input  Store,
  input  Clock,
  output [15:0] out_4
);

  _1_Bit_Register u_1_bit_register_1 (.Data(Data[0]), .Store(Store), .Clock(Clock), .out_4(out_4[0]));
  _1_Bit_Register u_1_bit_register_2 (.Data(Data[1]), .Store(Store), .Clock(Clock), .out_4(out_4[1]));
  _1_Bit_Register u_1_bit_register_3 (.Data(Data[2]), .Store(Store), .Clock(Clock), .out_4(out_4[2]));
  _1_Bit_Register u_1_bit_register_4 (.Data(Data[3]), .Store(Store), .Clock(Clock), .out_4(out_4[3]));
  _1_Bit_Register u_1_bit_register_5 (.Data(Data[4]), .Store(Store), .Clock(Clock), .out_4(out_4[4]));
  _1_Bit_Register u_1_bit_register_6 (.Data(Data[5]), .Store(Store), .Clock(Clock), .out_4(out_4[5]));
  _1_Bit_Register u_1_bit_register_7 (.Data(Data[6]), .Store(Store), .Clock(Clock), .out_4(out_4[6]));
  _1_Bit_Register u_1_bit_register_8 (.Data(Data[7]), .Store(Store), .Clock(Clock), .out_4(out_4[7]));
  _1_Bit_Register u_1_bit_register_9 (.Data(Data[8]), .Store(Store), .Clock(Clock), .out_4(out_4[8]));
  _1_Bit_Register u_1_bit_register_10 (.Data(Data[9]), .Store(Store), .Clock(Clock), .out_4(out_4[9]));
  _1_Bit_Register u_1_bit_register_11 (.Data(Data[10]), .Store(Store), .Clock(Clock), .out_4(out_4[10]));
  _1_Bit_Register u_1_bit_register_12 (.Data(Data[11]), .Store(Store), .Clock(Clock), .out_4(out_4[11]));
  _1_Bit_Register u_1_bit_register_13 (.Data(Data[12]), .Store(Store), .Clock(Clock), .out_4(out_4[12]));
  _1_Bit_Register u_1_bit_register_14 (.Data(Data[13]), .Store(Store), .Clock(Clock), .out_4(out_4[13]));
  _1_Bit_Register u_1_bit_register_15 (.Data(Data[14]), .Store(Store), .Clock(Clock), .out_4(out_4[14]));
  _1_Bit_Register u_1_bit_register_16 (.Data(Data[15]), .Store(Store), .Clock(Clock), .out_4(out_4[15]));
endmodule

module RAM8 (
  input  [15:0] Data,
  input  [2:0] Address,
  input  Store,
  input  Clk,
  output [15:0] Out
);

  wire demultiplexer_1_out0, demultiplexer_1_out1, demultiplexer_1_out2, demultiplexer_1_out3,
       demultiplexer_1_out4, demultiplexer_1_out5, demultiplexer_1_out6, demultiplexer_1_out7;
  wire [15:0] n16_bit_register_1_out_4, n16_bit_register_2_out_4, n16_bit_register_3_out_4,
       n16_bit_register_4_out_4, n16_bit_register_5_out_4, n16_bit_register_6_out_4,
       n16_bit_register_7_out_4, n16_bit_register_8_out_4;

  Demultiplexer #(.select(3)) demultiplexer_1 (
    .out0(demultiplexer_1_out0), .out1(demultiplexer_1_out1), .out2(demultiplexer_1_out2),
    .out3(demultiplexer_1_out3), .out4(demultiplexer_1_out4), .out5(demultiplexer_1_out5),
    .out6(demultiplexer_1_out6), .out7(demultiplexer_1_out7), .in(Store), .sel(Address), .en(Store));
  _16_Bit_Register u_16_bit_register_1 (
    .Data(Data), .Store(demultiplexer_1_out0), .Clock(Clk), .out_4(n16_bit_register_1_out_4));
  _16_Bit_Register u_16_bit_register_2 (
    .Data(Data), .Store(demultiplexer_1_out1), .Clock(Clk), .out_4(n16_bit_register_2_out_4));
  _16_Bit_Register u_16_bit_register_3 (
    .Data(Data), .Store(demultiplexer_1_out2), .Clock(Clk), .out_4(n16_bit_register_3_out_4));
  _16_Bit_Register u_16_bit_register_4 (
    .Data(Data), .Store(demultiplexer_1_out3), .Clock(Clk), .out_4(n16_bit_register_4_out_4));
  _16_Bit_Register u_16_bit_register_5 (
    .Data(Data), .Store(demultiplexer_1_out4), .Clock(Clk), .out_4(n16_bit_register_5_out_4));
  _16_Bit_Register u_16_bit_register_6 (
    .Data(Data), .Store(demultiplexer_1_out5), .Clock(Clk), .out_4(n16_bit_register_6_out_4));
  _16_Bit_Register u_16_bit_register_7 (
    .Data(Data), .Store(demultiplexer_1_out6), .Clock(Clk), .out_4(n16_bit_register_7_out_4));
  _16_Bit_Register u_16_bit_register_8 (
    .Data(Data), .Store(demultiplexer_1_out7), .Clock(Clk), .out_4(n16_bit_register_8_out_4));
  Multiplexer #(.select(3), .width(16)) multiplexer_1 (
    .in0(n16_bit_register_1_out_4), .in1(n16_bit_register_2_out_4), .in2(n16_bit_register_3_out_4),
    .in3(n16_bit_register_4_out_4), .in4(n16_bit_register_5_out_4), .in5(n16_bit_register_6_out_4),
    .in6(n16_bit_register_7_out_4), .in7(n16_bit_register_8_out_4), .out(Out), .sel(Address), .en(1'b1));

  // Notes on the sheet:
  //   |Address| = log2(8) = 3
  //   To route the store signal to the correct register, so the correct data is stored, you have to make a Dmux(8) gate, and then use a Mux(8) gate to send the correct register output to the output pin based off of the same address input
endmodule

module RAM64 (
  input  [15:0] Data,
  input  [5:0] Address,
  input  Store,
  input  Clk,
  output [15:0] Out
);

  wire demultiplexer_1_out0, demultiplexer_1_out1, demultiplexer_1_out2, demultiplexer_1_out3,
       demultiplexer_1_out4, demultiplexer_1_out5, demultiplexer_1_out6, demultiplexer_1_out7;
  wire [15:0] ram8_1_out, ram8_2_out, ram8_3_out, ram8_4_out, ram8_5_out, ram8_6_out, ram8_7_out, ram8_8_out;

  Demultiplexer #(.select(3)) demultiplexer_1 (
    .out0(demultiplexer_1_out0), .out1(demultiplexer_1_out1), .out2(demultiplexer_1_out2),
    .out3(demultiplexer_1_out3), .out4(demultiplexer_1_out4), .out5(demultiplexer_1_out5),
    .out6(demultiplexer_1_out6), .out7(demultiplexer_1_out7), .in(Store), .sel(Address[5:3]), .en(1'b1));
  RAM8 ram8_1 (.Data(Data), .Address(Address[2:0]), .Store(demultiplexer_1_out0), .Clk(Clk), .Out(ram8_1_out));
  RAM8 ram8_2 (.Data(Data), .Address(Address[2:0]), .Store(demultiplexer_1_out1), .Clk(Clk), .Out(ram8_2_out));
  RAM8 ram8_3 (.Data(Data), .Address(Address[2:0]), .Store(demultiplexer_1_out2), .Clk(Clk), .Out(ram8_3_out));
  RAM8 ram8_4 (.Data(Data), .Address(Address[2:0]), .Store(demultiplexer_1_out3), .Clk(Clk), .Out(ram8_4_out));
  RAM8 ram8_5 (.Data(Data), .Address(Address[2:0]), .Store(demultiplexer_1_out4), .Clk(Clk), .Out(ram8_5_out));
  RAM8 ram8_6 (.Data(Data), .Address(Address[2:0]), .Store(demultiplexer_1_out5), .Clk(Clk), .Out(ram8_6_out));
  RAM8 ram8_7 (.Data(Data), .Address(Address[2:0]), .Store(demultiplexer_1_out6), .Clk(Clk), .Out(ram8_7_out));
  RAM8 ram8_8 (.Data(Data), .Address(Address[2:0]), .Store(demultiplexer_1_out7), .Clk(Clk), .Out(ram8_8_out));
  Multiplexer #(.select(3), .width(16)) multiplexer_1 (
    .in0(ram8_1_out), .in1(ram8_2_out), .in2(ram8_3_out), .in3(ram8_4_out), .in4(ram8_5_out),
    .in5(ram8_6_out), .in6(ram8_7_out), .in7(ram8_8_out), .out(Out), .sel(Address[5:3]), .en(1'b1));

  // Other names for the same wires on the sheet: Addr[2:0] = Address[5:3]

  // Notes on the sheet:
  //   |Address| = log2(64) = 6
  //   Note: last 3 bits of address can be used to address 1 of the 8 individual registers within each RAM8, rest of address bits used in multiplexer to select RAM8 chip
endmodule

module RAM512 (
);


  // Notes on the sheet:
  //   Implement 512, 4k, and 16k in the same way as you implemented RAM64 out of RAM8
endmodule

module RAM4K (
);


  // Notes on the sheet:
  //   Implement 512, 4k, and 16k in the same way as you implemented RAM64 out of RAM8
endmodule

module RAM16K (
);


  // Notes on the sheet:
  //   Implement 512, 4k, and 16k in the same way as you implemented RAM64 out of RAM8
endmodule
